// Logisim project circuit.circ as structural Verilog: 6 circuits, main circuit MAXV_CHENILLARD
module MAXV_CHENILLARD (
  input  pulse_load_i,
  input  load_i,
  input  [7:0] switch_i,
  input  clk_i,
  input  nReset_i,
  output [7:0] led_o
);

  wire entree_i_sw7, entree_i_sw8, not_1_out;
  wire [1:0] entree_i_sw2;

  DipSwitch entree_i (
    .sw1(entree_i_sw2[1]), .sw2(entree_i_sw2[0]), .sw7(entree_i_sw7), .sw8(entree_i_sw8));  // open: sw3, sw4, sw5, sw6
  not not_1 (not_1_out, nReset_i);
  chenillard_TOP chenillard_TOP_1 (
    .pulse_Load_i(pulse_load_i), .load_i(load_i), .enable_i(entree_i_sw7), .right_nleft_i(entree_i_sw8),
    .speed_i(entree_i_sw2), .val_i(switch_i), .clk_i(clk_i), .reset_i(not_1_out), .led_o(led_o));

  // Notes on the sheet:
  //   Attention, votre version de Logisim
  //   ne contient pas de tracker. Si vous
  //   enregistrez votre projet, toutes les
  //   informations du tracker seront
  //   définitivement effacées.
endmodule

module chenillard_TOP (
  input  pulse_Load_i,
  input  load_i,
  input  enable_i,
  input  right_nleft_i,
  input  [1:0] speed_i,
  input  [7:0] val_i,
  input  clk_i,
  input  reset_i,
  output [7:0] led_o
);

  wire and_1_out, Bascule_RS_1_q_o, Bascule_RS_2_q_o, clk_i_t, demultiplexer_1_out0, demultiplexer_1_out1,
       done_o, not_1_out, or_1_out, or_2_out, or_4_out, or_5_out;
  wire [1:0] mode_i;
  wire [27:0] multiplexer_1_out;

  Clock test_clk (.out(clk_i_t));
  Clock sysclk ();  // open: out
  Multiplexer #(.select(2), .width(28), .enable("false")) multiplexer_1 (
    .in0(28'h2), .in1(28'he4e1bf), .in2(28'h1c9c37f), .in3(28'h39386ff), .out(multiplexer_1_out),
    .sel(speed_i));
  Demultiplexer #(.enable("false")) demultiplexer_1 (
    .out0(demultiplexer_1_out0), .out1(demultiplexer_1_out1), .in(pulse_Load_i), .sel(right_nleft_i));
  or or_1 (or_1_out, led_o[0], reset_i);
  or or_2 (or_2_out, led_o[7], reset_i);
  and and_1 (and_1_out, right_nleft_i, done_o, enable_i);
  not not_1 (not_1_out, load_i);
  or or_3 (mode_i[0], load_i, and_1_out);
  and and_2 (mode_i[1], not_1_out, done_o, enable_i);
  timer_28b timer_28b_1 (
    .value_i(multiplexer_1_out), .en_i(1'b1), .load_i(done_o), .clk_i(clk_i_t), .reset_i(reset_i),
    .done_o(done_o));
  Bascule_RS Bascule_RS_2 (.S_i(demultiplexer_1_out0), .R_i(or_1_out), .Q_o(Bascule_RS_2_q_o));
  Bascule_RS Bascule_RS_1 (.S_i(demultiplexer_1_out1), .R_i(or_2_out), .Q_o(Bascule_RS_1_q_o));
  or or_4 (or_4_out, Bascule_RS_2_q_o, led_o[7]);
  or or_5 (or_5_out, Bascule_RS_1_q_o, led_o[0]);
  shift_reg_8b shift_reg_8b_1 (
    .ser_l_i(or_4_out), .ser_r_i(or_5_out), .value_load_i(val_i), .mode_i(mode_i), .clk_i(clk_i_t),
    .reset_i(reset_i), .val_o(led_o));

  // Other names for the same wires on the sheet: out_lsb = led_o[0]; out_msb = led_o[7]; rst = reset_i

  // Notes on the sheet:
  //   Attention, votre version de Logisim
  //   ne contient pas de tracker. Si vous
  //   enregistrez votre projet, toutes les
  //   informations du tracker seront
  //   définitivement effacées.
endmodule

module shift_reg_4b (
  input  ser_r_i,
  input  ser_l_i,
  input  [3:0] value_load_i,
  input  [1:0] mode_i,
  input  clk_i,
  input  reset_i,
  output [3:0] val_o
);

  wire multiplexer_1_out, multiplexer_2_out, multiplexer_3_out, multiplexer_4_out;

  Multiplexer #(.select(2), .enable("false")) multiplexer_1 (
    .in0(val_o[3]), .in1(value_load_i[3]), .in2(val_o[2]), .in3(ser_r_i), .out(multiplexer_1_out),
    .sel(mode_i));
  D_Flip_Flop d_ff_1 (.D(multiplexer_1_out), .clk(clk_i), .Q(val_o[3]), .preset(1'b0), .reset(reset_i));  // open: Qn
  Multiplexer #(.select(2), .enable("false")) multiplexer_2 (
    .in0(val_o[2]), .in1(value_load_i[2]), .in2(val_o[1]), .in3(val_o[3]), .out(multiplexer_2_out),
    .sel(mode_i));
  D_Flip_Flop d_ff_2 (.D(multiplexer_2_out), .clk(clk_i), .Q(val_o[2]), .preset(1'b0), .reset(reset_i));  // open: Qn
  Multiplexer #(.select(2), .enable("false")) multiplexer_3 (
    .in0(val_o[1]), .in1(value_load_i[1]), .in2(val_o[0]), .in3(val_o[2]), .out(multiplexer_3_out),
    .sel(mode_i));
  D_Flip_Flop d_ff_3 (.D(multiplexer_3_out), .clk(clk_i), .Q(val_o[1]), .preset(1'b0), .reset(reset_i));  // open: Qn
  Multiplexer #(.select(2), .enable("false")) multiplexer_4 (
    .in0(val_o[0]), .in1(value_load_i[0]), .in2(ser_l_i), .in3(val_o[1]), .out(multiplexer_4_out),
    .sel(mode_i));
  D_Flip_Flop d_ff_4 (.D(multiplexer_4_out), .clk(clk_i), .Q(val_o[0]), .preset(1'b0), .reset(reset_i));  // open: Qn

  // Other names for the same wires on the sheet: L = ser_l_i; R = ser_r_i; Q0 = val_o[0]; Q1 = val_o[1];
  //   Q2 = val_o[2]; Q3 = val_o[3]; D0 = value_load_i[0]; D1 = value_load_i[1]; D2 = value_load_i[2];
  //   D3 = value_load_i[3]

  // Notes on the sheet:
  //   Attention, votre version de Logisim
  //   ne contient pas de tracker. Si vous
  //   enregistrez votre projet, toutes les
  //   informations du tracker seront
  //   définitivement effacées.
endmodule

module shift_reg_8b (
  input  ser_l_i,
  input  ser_r_i,
  input  [7:0] value_load_i,
  input  [1:0] mode_i,
  input  clk_i,
  input  reset_i,
  output [7:0] val_o
);

  Clock test_clk ();  // open: out
  Clock sysclk ();  // open: out
  shift_reg_4b shift_reg_4b_1 (
    .ser_r_i(ser_r_i), .ser_l_i(val_o[3]), .value_load_i(value_load_i[7:4]), .mode_i(mode_i), .clk_i(clk_i),
    .reset_i(reset_i), .val_o(val_o[7:4]));
  shift_reg_4b shift_reg_4b_2 (
    .ser_r_i(val_o[4]), .ser_l_i(ser_l_i), .value_load_i(value_load_i[3:0]), .mode_i(mode_i), .clk_i(clk_i),
    .reset_i(reset_i), .val_o(val_o[3:0]));

  // Other names for the same wires on the sheet: val_0_3_o[3:0] = val_o[3:0]; val_3_o = val_o[3];
  //   val_4_7_o[3:0] = val_o[7:4]; val_4_o = val_o[4]; value_load_0_3_i[3:0] = value_load_i[3:0];
  //   value_load_4_7_i[3:0] = value_load_i[7:4]

  // Notes on the sheet:
  //   Attention, votre version de Logisim
  //   ne contient pas de tracker. Si vous
  //   enregistrez votre projet, toutes les
  //   informations du tracker seront
  //   définitivement effacées.
endmodule

module timer_28b (
  input  [27:0] value_i,
  input  en_i,
  input  load_i,
  input  clk_i,
  input  reset_i,
  output done_o
);

  wire [27:0] multiplexer_1_out, multiplexer_2_out, Q, subtractor_1_out;

  Subtractor #(.width(28)) subtractor_1 (.a(Q), .b(28'h1), .out(subtractor_1_out), .bin(1'b0));  // open: bout
  Multiplexer #(.width(28), .enable("false")) multiplexer_1 (
    .in0(Q), .in1(subtractor_1_out), .out(multiplexer_1_out), .sel(en_i));
  Multiplexer #(.width(28), .enable("false")) multiplexer_2 (
    .in0(multiplexer_1_out), .in1(value_i), .out(multiplexer_2_out), .sel(load_i));
  Register #(.width(28)) register_1 (.D(multiplexer_2_out), .en(1'b1), .clk(clk_i), .Q(Q), .clr(reset_i));
  Comparator #(.width(28)) comparator_1 (.a(Q), .b({28{1'b0}}), .eq(done_o));  // open: gt, lt

  // Notes on the sheet:
  //   Attention, votre version de Logisim
  //   ne contient pas de tracker. Si vous
  //   enregistrez votre projet, toutes les
  //   informations du tracker seront
  //   définitivement effacées.
endmodule

module Bascule_RS (
  input  S_i,
  input  R_i,
  output Q_o
);

  wire nor_1_out, nor_2_out;

  nor nor_1 (nor_1_out, S_i, nor_2_out);
  nor nor_2 (nor_2_out, nor_1_out, R_i);
  not not_1 (Q_o, nor_1_out);

  // Notes on the sheet:
  //   Attention, votre version de Logisim
  //   ne contient pas de tracker. Si vous
  //   enregistrez votre projet, toutes les
  //   informations du tracker seront
  //   définitivement effacées.
endmodule
